# Fritzing sketch ControllerBoard (saved by Fritzing 0.9.10b)
perfboards: 1

parts:
  J1 = female pin header, 6 pins [form="♀ (female)"]
  WeMos_D1_Mini1 = WeMos D1 Mini
  R1 = Photocell (LDR) [package=THT]
  J2 = female pin header, 3 pins [form="♀ (female)"]
  R2 = Resistor [tolerance=±5% power=0.25 resistance=10k package=THT]
  S1 = Pushbutton [package="[THT]"]
  S2 = Pushbutton [package="[THT]"]
  Bauteil1 = ws2812b [package="smd 2812b"]

nets:
  N1: J1.pin1, WeMos_D1_Mini1.A0, R1.pin_0, R2.Pin_1
  N2: J1.pin2, WeMos_D1_Mini1.3V3, R1.pin_1
  N3: J1.pin3, J1.pin4, WeMos_D1_Mini1.G, J2.pin1, R2.Pin_0, S1.Pin_1, S1.Pin_2, S2.Pin_1, S2.Pin_2, Bauteil1.VSS
  N4: J1.pin5, WeMos_D1_Mini1.D2, S1.Pin_3, S1.Pin_4
  N5: J1.pin6, WeMos_D1_Mini1.D1, S2.Pin_3, S2.Pin_4
  5V: WeMos_D1_Mini1.5V, J2.pin3, Bauteil1.VDD
  N6: WeMos_D1_Mini1.D3, J2.pin2, Bauteil1.DIN
